# Fritzing sketch ArduinoClock (saved by Fritzing 0.9.3b)
circuit board: 8.46667cm x 5.64444cm
breadboards: 1

parts:
  WeMos_D1_Mini1 = WeMos D1 Mini
  SR1 = 74HC595 [package="DIP16 [THT]"]
  SR2 = 74HC595 [package="DIP16 [THT]"]
  S1 = Pushbutton [package="[THT]"]
  RTC = Real Time Clock Module - DS1307 RTC Breakout Board
  7_Segment_4_Digit_Display = 7-SEGMENT-4DIGIT common cathode [part_number=HS420561K-32 package=7-segment-4digit-cathode]
  Piezo1 = Piezo Speaker - PC Mount [part_number=COM-07950]

nets:
  5V: WeMos_D1_Mini1.5V, SR1.MR, SR1.OE, SR1.VCC, SR2.MR, SR2.VCC, RTC.5V
  N1: WeMos_D1_Mini1.D0, S1.Pin_3, S1.Pin_4
  N2: WeMos_D1_Mini1.D1, RTC.SCL
  N3: WeMos_D1_Mini1.D2, RTC.SDA
  N4: WeMos_D1_Mini1.D5, Piezo1.VCC
  N5: WeMos_D1_Mini1.D6, SR1.DS
  N6: WeMos_D1_Mini1.D7, SR1.ST_CP, SR2.ST_CP
  N7: WeMos_D1_Mini1.D8, SR1.SH_CP, SR2.SH_CP
  GND: WeMos_D1_Mini1.G, SR1.GND, SR2.GND, SR2.OE, S1.Pin_1, S1.Pin_2, RTC.GND, Piezo1.GND
  N8: SR1.Q1, 7_Segment_4_Digit_Display.pin_7
  N9: SR1.Q2, 7_Segment_4_Digit_Display.pin_4
  N10: SR1.Q3, 7_Segment_4_Digit_Display.pin_2
  N11: SR1.Q4, 7_Segment_4_Digit_Display.pin_1
  N12: SR1.Q5, 7_Segment_4_Digit_Display.pin_10
  N13: SR1.Q6, 7_Segment_4_Digit_Display.pin_5
  N14: SR1.Q7, 7_Segment_4_Digit_Display.pin_3
  N15: SR1.Q7', SR2.DS
  N16: SR1.Q0, 7_Segment_4_Digit_Display.pin_11
  N17: SR2.Q1, 7_Segment_4_Digit_Display.pin_9
  N18: SR2.Q2, 7_Segment_4_Digit_Display.pin_8
  N19: SR2.Q3, 7_Segment_4_Digit_Display.pin_6
  N20: SR2.Q0, 7_Segment_4_Digit_Display.pin_12

notes:
  ArduinoClock
  Designed by: Ameer Dawood

custom parts:
  WeMos D1 Mini: The D1 mini is a mini wifi board based on ESP-8266EX.
  7-SEGMENT-4DIGIT common cathode: A 7 Segment 4 Digit common cathode display, with decimal points
  Piezo Speaker - PC Mount: This is a small 12mm round speaker that operates around the audible 2kHz range. You can use these speakers to create simple music or user interfaces. Each speaker is PTH solderable and requires an operating voltage of 3.5-5V with a mean current of 35mA max. These speakers also have a typical sound output of 95 dBA and a coil resistance of 42 ±6.3 ohms.
